# Fritzing sketch Esquematico (saved by Fritzing 0.9.3b)
breadboards: 1

parts:
  Arduino_UNO1 = Arduino Uno (Rev3)
  SP1 = SPEAKER [package=pcb_mount_speaker]
  R3 = Resistor [tolerance=±5% resistance=220 package="0402 [SMD]"]
  R2 = Resistor [tolerance=±5% resistance=10k package="0402 [SMD]"]
  R4 = Photocell (LDR) [package=THT]

nets:
  N1: Arduino_UNO1.A0, R2.Pin_0, R4.pin_1
  N2: Arduino_UNO1.D9_PWM, R3.Pin_0
  GND: Arduino_UNO1.GND, SP1.+, R4.pin_0
  5V: Arduino_UNO1.5V, R2.Pin_1
  N3: SP1.-, R3.Pin_1
