# Fritzing sketch mic_leds (saved by Fritzing 0.9.3b)
breadboards: 1

parts:
  Parte1 = Arduino Uno (Rev3)
  Parte2 = Breakout Board for Electret Microphone
  R1 = Resistor [tolerance=±5% resistance=220 package=THT]
  LED1 = LEDs [package=led10mm]
  R2 = Resistor [tolerance=±5% resistance=220 package=THT]
  R3 = Resistor [tolerance=±5% resistance=220 package=THT]
  R4 = Resistor [tolerance=±5% resistance=220 package=THT]
  R5 = Resistor [tolerance=±5% resistance=220 package=THT]
  LED2 = LEDs [package=led10mm]
  LED3 = LEDs [package=led10mm]
  LED4 = LEDs [package=led10mm]
  LED5 = LEDs [package=led10mm]

nets:
  N1: Parte1.A0, Parte2.AUD
  GND: Parte1.GND, Parte2.GND, LED1.C, LED2.C, LED3.C, LED4.C, LED5.C
  N2: Parte1.D2, R5.Pin_1
  N3: Parte1.D3_PWM, R4.Pin_1
  N4: Parte1.D4, R3.Pin_1
  N5: Parte1.D5_PWM, R2.Pin_1
  N6: Parte1.D6_PWM, R1.Pin_1
  5V: Parte1.5V, Parte2.VCC
  N7: R1.Pin_0, LED1.A
  N8: R2.Pin_0, LED2.A
  N9: R3.Pin_0, LED3.A
  N10: R4.Pin_0, LED4.A
  N11: R5.Pin_0, LED5.A
