# Fritzing sketch HCSR04_MOTOR (saved by Fritzing 0.8.7b)
breadboards: 1

parts:
  Parte1 = Arduino Uno (Rev3)
  U3 = HC-SR04 [chip_label=IC package="SIP (Single Inline) [THT]"]
  Q1 = NPN-Transistor [package="TO92 [THT]"]
  R1 = Resistor [tolerance=±5% resistance=220 package=THT]
  M1 = DC Motor
  D2 = Schottky Diode [part_number=1N5817 package="Melf DO-213 AB [SMD]"]

nets:
  N1: Parte1.D9_PWM, R1.Pin_0
  Trigger: Parte1.D12/MISO, U3.Trig
  Echo: Parte1.D13/SCK, U3.Echo
  5V/VCC: Parte1.5V, U3.Vcc, M1.pin_1, D2.cathode
  GND: Parte1.GND, U3.GND, Q1.E
  N2: Q1.B, R1.Pin_1
  N3: Q1.C, M1.pin_2, D2.anode

custom parts:
  HC-SR04: HC-SR04 ultrasound distance sensor
